// Logisim project registro.circ as structural Verilog: 2 circuits, main circuit main
module main (
  input  CLK,
  input  \input ,
  input  clear,
  input  D1,
  input  D2,
  input  D3,
  input  D4,
  input  [1:0] Accionador,
  output out_9,
  output out_10,
  output out_11,
  output out_12
);

  wire multiplexer_1_out, multiplexer_2_out, multiplexer_3_out, multiplexer_4_out;

  Multiplexer #(.select(2)) multiplexer_1 (
    .in0(\input ), .in1(out_10), .in2(D1), .in3(out_9), .out(multiplexer_1_out), .sel(Accionador));  // open: en
  D_Flip_Flop d_ff_1 (.clk(CLK), .D(multiplexer_1_out), .Q(out_9), .reset(clear));  // open: Qn, preset, en
  D_Flip_Flop d_ff_2 (.clk(CLK), .D(multiplexer_2_out), .Q(out_10), .reset(clear));  // open: Qn, preset, en
  Multiplexer #(.select(2)) multiplexer_2 (
    .in0(out_9), .in1(out_11), .in2(D2), .in3(out_10), .out(multiplexer_2_out), .sel(Accionador));  // open: en
  Multiplexer #(.select(2)) multiplexer_3 (
    .in0(out_10), .in1(out_12), .in2(D3), .in3(out_11), .out(multiplexer_3_out), .sel(Accionador));  // open: en
  D_Flip_Flop d_ff_3 (.clk(CLK), .D(multiplexer_3_out), .Q(out_11), .reset(clear));  // open: Qn, preset, en
  Multiplexer #(.select(2)) multiplexer_4 (
    .in0(out_11), .in2(D4), .in3(out_12), .out(multiplexer_4_out), .sel(Accionador));  // open: in1, en
  D_Flip_Flop d_ff_4 (.clk(CLK), .D(multiplexer_4_out), .Q(out_12), .reset(clear));  // open: Qn, preset, en

  // Notes on the sheet:
  //   00 derecha
  //   01 Izquierda
  //   10 carga
  //   11 mantenimiento
endmodule

module Ej_3 (
  input  in_1,
  input  in_2,
  output out_3,
  output out_4,
  output out_5,
  output out_6
);

  wire a1, a2, a3, and_1_out, d_ff_1_qn, d_ff_2_qn, d_ff_3_qn;
  wire [0:0] a3_out;

  and and_1 (and_1_out, ~a1, a2, a3);  // AND_Gate
  or u_a3 (a3_out[0], a1, a3);
  D_Flip_Flop d_ff_1 (.clk(in_2), .D(d_ff_1_qn), .Q(a1), .Qn(d_ff_1_qn));  // open: preset, en, reset
  main main_1 (
    .\input (in_1), .clear(and_1_out), .Accionador({a2, a3_out[0]}), .CLK(in_2), .out_9(out_3),
    .out_10(out_4), .out_11(out_5), .out_12(out_6));  // open: D2, D3, D4, D1
  D_Flip_Flop d_ff_2 (.clk(d_ff_1_qn), .D(d_ff_2_qn), .Q(a2), .Qn(d_ff_2_qn));  // open: preset, en, reset
  D_Flip_Flop d_ff_3 (.clk(d_ff_2_qn), .D(d_ff_3_qn), .Q(a3), .Qn(d_ff_3_qn));  // open: preset, en, reset
endmodule
