// Logisim project 3.2.circ as structural Verilog: 1 circuit, main circuit main
module main (
  input  [3:0] in_1,
  input  [3:0] in_2,
  input  in_3,
  input  C1_C2
);

  wire adder_1_cout, and_1_out;
  wire [3:0] xor_1_out;

  Adder #(.width(4)) adder_1 (.a(in_1), .b(xor_1_out), .cin(and_1_out), .cout(adder_1_cout));  // open: out
  assign xor_1_out = {4{in_3}} ^ in_2;  // XOR_Gate xor_1, 4 bits wide
  and and_1 (and_1_out, C1_C2, in_3);
  // OR_Gate or_1 has open pins: in0=adder_1_cout, in1=C1_C2, out=open
endmodule
