// Logisim project Ej3.circ as structural Verilog: 1 circuit, main circuit main
module main (
  input  [3:0] in_1,
  input  [3:0] in_2,
  input  in_3,
  input  in_4,
  input  in_5,
  output [3:0] out_6
);

  wire [3:0] RESSUM;

  Adder #(.width(4)) adder_1 (.a(in_1), .b(in_2), .out(RESSUM));  // open: cin, cout
  Multiplexer #(.width(4)) multiplexer_1 (.in0(RESSUM), .out(out_6), .sel(in_3));  // open: in1, en

  assign in_5 = in_4;

  // Other names for the same wires on the sheet: SUM[3:0] = in_1; SUM2[3:0] = in_2
endmodule
